# Fritzing sketch netchk (saved by Fritzing 0.9.3b)
circuit board: 2.56cm x 3.42cm

parts:
  J1 = male pin header, 8 pins [form="♂ (male)"]
  J2 = male pin header, 8 pins [form="♂ (male)"]
  LED2 = RGB LED (com. cathode, rgb) [package="5 mm [THT]"]
  LED4 = RGB LED (com. cathode, rgb) [package="5 mm [THT]"]
  LED3 = RGB LED (com. cathode, rgb) [package="5 mm [THT]"]
  LED1 = RGB LED (com. cathode, rgb) [package="5 mm [THT]"]
  Piezo = Piezo Speaker

nets:
  N1: J1.pin7, Piezo.pin2
  N2: J2.pin3, LED2.red_anode, LED4.red_anode, LED3.red_anode, LED1.red_anode
  N3: J2.pin4, LED2.green_anode, LED4.green_anode, LED3.green_anode, LED1.green_anode
  N4: J2.pin6, LED2.blue_anode, LED4.blue_anode, LED3.blue_anode, LED1.blue_anode
  N5: J2.pin7, LED2.common_cathode, LED4.common_cathode, LED3.common_cathode, LED1.common_cathode, Piezo.pin1

notes:
  NetCheck
